# Fritzing sketch dust (saved by Fritzing 0.9.3b)
circuit board: 8.46667cm x 5.64444cm
breadboards: 1

parts:
  J1 = male pin header, 4 pins [form="♂ (male)"]
  C1 = Electrolytic Capacitor [capacitance=220µF package="100 mil [THT, electrolytic]"]
  IC1 = IC, SIP package, 6 pins [chip_label=GP2Y1010AU0F]
  R1 = Resistor [tolerance=±5% resistance=150 package=THT]

nets (from the schematic view):
  N1: J1.pin1, IC1.pin6
  N2: J1.pin2, C1.+, IC1.pin2, IC1.pin4
  N3: J1.pin3, IC1.pin3
  N4: J1.pin4, IC1.pin5
  N5: C1.-, IC1.pin1, R1.Pin_1

notes:
  5V - Vo - LED - GND
