# Fritzing sketch esp-12 (saved by Fritzing 0.9.3b)

parts:
  U2 = IC, DIP package, 20 pins [chip_label=SN74HC245]
  J1 = female pin header, 8 pins [form="♀ (female)"]
  U1 = ESP8266-12 WiFi Module [part_number=ESP8266]

nets:
  N1: U2.pin1, U2.pin10, U2.pin19, J1.pin8, U1.GND
  N2: U2.pin2, U1.RESET
  N3: U2.pin3, U1.ADC
  N4: U2.pin4, U1.GPIO_2
  N5: U2.pin5, U1.GPIO_0
  N6: U2.pin6, U1.RXD
  N7: U2.pin14, J1.pin6
  N8: U2.pin15, J1.pin5
  N9: U2.pin16, J1.pin4
  N10: U2.pin17, J1.pin3
  N11: U2.pin18, J1.pin2
  N12: U2.pin20, J1.pin1, U1.VCC
  N13: J1.pin7, U1.TXD

notes:
  3v3 - RST - CHPD - GPIO2 - GPIO0 - RX - TX

custom parts:
  ESP8266-12 WiFi Module: Generic WiFi Module based on the ESP8266 with onboard PCB antenna and UART communications
