# Fritzing sketch general (saved by Fritzing 0.9.3b)
circuit board: 8.46667cm x 5.64444cm
breadboards: 1

parts:
  Part1 = Arduino Nano (Rev3.0) (ICSP)
  U1 = ESP8266 WiFi Module [part_number=ESP8266]
  IC1 = IC, SIP package, 4 pins [chip_label=LCDI2C]
  DHT1 = DHT22 Humidity and Temperature Sensor
  IC2 = IC, SIP package, 4 pins [chip_label=GP2Y]
  Part3 = MQ-7 breakout
  IC3 = IC, SIP package, 3 pins [chip_label=Piezo]
  IC4 = IC, SIP package, 5 pins [chip_label=LED]

nets (from the breadboard view):
  GND: Part1.GND, U1.GND, IC1.pin4, DHT1.GND, IC2.pin2, Part3.GND, IC3.pin3, IC4.pin5
  N1: Part1.D2, IC2.pin3
  N2: Part1.D3, U1.RXD
  N3: Part1.D4, U1.TXD
  N4: Part1.D5, IC3.pin2
  N5: Part1.D6, IC4.pin2
  N6: Part1.D7, IC4.pin3
  N7: Part1.D9, IC4.pin4
  N8: Part1.D10, DHT1.DATA
  VIN: Part1.VIN, IC1.pin3, DHT1.VDD, IC2.pin1, Part3.VCC, IC3.pin1, IC4.pin1
  N9: Part1.A5, IC1.pin1
  N10: Part1.A4, IC1.pin2
  N11: Part1.A3, IC2.pin4
  N12: Part1.A2, Part3.DO
  3V3: Part1.3V3, U1.VCC, U1.RST, U1.CH_PD

custom parts:
  ESP8266 WiFi Module: Generic WiFi Module based on the ESP8266 with onboard PCB antenna and UART communications
  MQ-7 breakout: SKU: 101282
