# Fritzing sketch led (saved by Fritzing 0.9.2b)
circuit board: 6.70848cm x 3.71952cm
breadboards: 1

parts:
  U1 = PCF8574 [package="DIP16 [THT]"]
  J1 = male pin header, 4 pins [form="♂ (male)"]
  LED1 = RGB LED (com. cathode, rbg) [package="5 mm [THT]"]
  LED2 = RGB LED (com. cathode, rbg) [package="5 mm [THT]"]
  R1 = Resistor [tolerance=±5% resistance=220 package=THT]
  R2 = Resistor [tolerance=±5% resistance=220 package=THT]
  R3 = Resistor [tolerance=±5% resistance=220 package=THT]
  R4 = Resistor [tolerance=±5% resistance=220 package=THT]
  R5 = Resistor [tolerance=±5% resistance=220 package=THT]
  R6 = Resistor [tolerance=±5% resistance=220 package=THT]

nets:
  N1: U1.P2, R1.Pin_0
  N2: U1.P3, R2.Pin_0
  N3: U1.GND, J1.pin2, LED1.common_cathode, LED2.common_cathode
  N4: U1.P4, R3.Pin_0
  N5: U1.P5, R4.Pin_0
  N6: U1.P6, R5.Pin_0
  N7: U1.P7, R6.Pin_0
  N8: U1.SCL, J1.pin4
  N9: U1.SDA, J1.pin3
  N10: U1.VCC, J1.pin1
  N11: LED1.red_anode, R1.Pin_1
  N12: LED1.blue_anode, R2.Pin_1
  N13: LED1.green_anode, R3.Pin_1
  N14: LED2.red_anode, R4.Pin_1
  N15: LED2.blue_anode, R5.Pin_1
  N16: LED2.green_anode, R6.Pin_1
