# Fritzing sketch led_74595 (saved by Fritzing 0.9.3b)
breadboards: 1

parts:
  LED1 = RGB LED (com. cathode, rbg) [package="5 mm [THT]"]
  LED2 = RGB LED (com. cathode, rbg) [package="5 mm [THT]"]
  R1 = Resistor [tolerance=±5% resistance=220 package="2010 [SMD]"]
  R2 = Resistor [tolerance=±5% resistance=220 package="2010 [SMD]"]
  R3 = Resistor [tolerance=±5% resistance=220 package="2010 [SMD]"]
  R4 = Resistor [tolerance=±5% resistance=220 package="2010 [SMD]"]
  R5 = Resistor [tolerance=±5% resistance=220 package="2010 [SMD]"]
  R6 = Resistor [tolerance=±5% resistance=220 package="2010 [SMD]"]
  U1 = 74HC595 SMD [package="SO16 [SMD]"]
  J1 = female pin header, 5 pins [form="♀ (female)"]

nets:
  N1: LED1.red_anode, R1.Pin_0
  N2: LED1.common_cathode, LED2.common_cathode, U1.GND, U1.OE, J1.pin5
  N3: LED1.blue_anode, R2.Pin_0
  N4: LED1.green_anode, R3.Pin_0
  N5: LED2.red_anode, R4.Pin_0
  N6: LED2.blue_anode, R5.Pin_0
  N7: LED2.green_anode, R6.Pin_0
  N8: R1.Pin_1, U1.Q1
  N9: R2.Pin_1, U1.Q2
  N10: R3.Pin_1, U1.Q3
  N11: R4.Pin_1, U1.Q5
  N12: R5.Pin_1, U1.Q6
  N13: R6.Pin_1, U1.Q7
  N14: U1.MR, U1.VCC, J1.pin1
  N15: U1.SH_CP, J1.pin4
  N16: U1.ST_CP, J1.pin3
  N17: U1.DS, J1.pin2

notes:
  5v - ds - st_cp - sh_cp - gnd
